# Fritzing sketch RasberryWiring (saved by Fritzing 0.9.3b)
breadboards: 1

parts:
  Composant1 = Arduino Nano (Rev3.0) (ICSP)
  Raspberry_Pi_1 = Raspberry Pi 3 [part_number=RPI-3-V1.2]
  M1 = BTS7960
  M2 = BTS7960

nets:
  N1: Composant1.D2, Composant1.D3, M1.pin1, M1.pin2
  N2: Composant1.D4, M2.pin1
  N3: Composant1.D5, M2.pin2
  N4: Composant1.D9, Raspberry_Pi_1.GPIO17
  GND: Composant1.D10, Composant1.GND, Raspberry_Pi_1.GND, M1.pin8, M2.pin8
  N5: Composant1.D11/MOSI, Raspberry_Pi_1.GPIO19
  N6: Composant1.D12/MISO, Raspberry_Pi_1.GPIO26
  VIN: Composant1.VIN, Raspberry_Pi_1.5V
  N7: Composant1.5V, M1.pin3, M1.pin4, M1.pin7, M2.pin3, M2.pin4, M2.pin7

notes:
  GPIO17
  GPIO12
  GPIO19
  GPIO26
  LEFT
  O --> GPIO19 <-> 9 <-> 3 <-> RPWM
  C --> GPIO26 <-> 10 <-> 2 <-> LPWM
  RIGHT
  O --> GPIO17 <-> 11 <-> 5 <-> RPWM
  C --> GPIO12 <-> 12 <-> 4 <-> LPWM

custom parts:
  BTS7960: BTS7960 43A Peak Power H-Bridge PWM Motor Driver
